# Fritzing sketch wiring_diagram (saved by Fritzing 0.9.10b)
breadboards: 1

parts:
  Part5 = Adafruit MAX98357A I2S 3W Class D Amplifier [part_number="Adafruit #3006"]
  Part7 = Adafruit Feather RP2040 [part_number="Adafruit #4884"]
  Part8 = Adafruit 2.0 inch 240x320 IPS TFT [part_number="Adafruit #4311"]
  Part9 = Adafruit FeatherWing Doubler [part_number="Adafruit #2890"]  # not connected
  BATT1 = LiPoly Battery (1300mAh)
  U1 = SWITCH_SPDT [package=kps-1290]
  Part10 = Adafruit I2C QT Rotary Encoder [part_number="Adafruit #4991"]

nets:
  N1: Part5.VIN, Part7.VBAT, BATT1.positive
  GND: Part5.GND, U1.S, Part10.GND
  N2: Part5.DIN, Part7.A3
  N3: Part5.BCLK, Part7.D24
  N4: Part5.LRCLK, Part7.D25
  N5: Part7.SDA, Part10.SDA
  N6: Part7.SCL, Part10.SCL
  N7: Part7.MISO, Part8.MOSI_5V
  N8: Part7.MOSI, Part8.MISO
  N9: Part7.SCK, Part8.SCLK_5V
  GND_2: Part7.GND, Part8.GND
  +3V3: Part7.+3V3, Part8.VIN
  N10: Part7.EN, U1.P
  N11: Part7.D13, Part8.SDCS_5V
  N12: Part7.D12, Part8.DC_5V
  N13: Part7.D11, Part8.RESET_5V
  N14: Part7.D10, Part8.LCDCS_5V

notes:
  D9 (neopixel)
  D5 (Key A)
  D6 (Key B),
  FeatherWing NeoKey
  Feather RP2040, FeatherWing NeoKey, and Amp are mounted on a Feather Doubler board

custom parts:
  Adafruit MAX98357A I2S 3W Class D Amplifier: Listen to this good news - we now have an all in one digital audio amp breakout board that works incredibly well with the Raspberry Pi! If you're looking for an easy and low cost way to get you digital sound files bumpin' then the MAX08357 I2S Amp Breakout is for you. It takes standard I2S digital audio input and, not only decodes it into analog, but also amplifies it directly into a speaker.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
  Adafruit Feather RP2040: A new chip means a new Feather, and the Raspberry Pi RP2040 is no exception. When we saw this chip we thought "this chip is going to be awesome when we give it the Feather Treatment" and so we did! This Feather features the RP2040, and all niceties you know and love about Feather Measures 2.0" x 0.9" x 0.28" (50.8mm x 22.8mm x 7mm) without headers soldered in Light as a (large?) feather - 5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
  Adafruit 2.0 inch 240x320 IPS TFT: This gorgeous IPS display breakout is the best way to add a small, colorful and bright display to any project, with excellent visibility from any angle. Since the display uses 4-wire SPI to communicate and has its own pixel-addressable frame buffer, it can be used with every kind of microcontroller. Even a very small one with low memory and few pins available! The 2.0" display has 320x240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
  Adafruit FeatherWing Doubler: This is the FeatherWing Doubler - a prototyping add-on and more for all Feather boards. This is similar to our FeatherWing Proto except there are two! The magic of the Doubler comes when stacking a Feather and another board on top of the Doubler so you can work with both boards simultaneously side-by-side! The Doubler, like the Proto, has a duplicate breakout for each pin on a Feather, as well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
  LiPoly Battery (1300mAh): Lithium Ion Polymer Battery (1300mAh)
  Adafruit I2C QT Rotary Encoder: Rotary encoders are soooo much fun! Twist em this way, then twist them that way. Unlike potentiometers, they go all the way around, and often have little detents for tactile feedback. But, if you've ever tried to add encoders to your project you know that they're a real challenge to use: timers, interrupts, debouncing... This Stemma QT breakout makes all that frustration go away - solder in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
